# Fritzing sketch WAC (saved by Fritzing 0.9.3b)
circuit board: 2.5cm x 4.7cm
breadboards: 1

parts:
  R1 = Resistor [tolerance=±5% resistance=1k package=THT]
  R2 = Resistor [tolerance=±5% resistance=22 package=THT]
  LED1 = LED - 5mm [color="Infrared (940nm)" package="5 mm [THT]"]
  Q1 = NPN-Transistor [package="TO92 [THT]"]
  J2 = female pin header, 8 pins [form="♀ (female)"]
  J1 = female pin header, 8 pins [form="♀ (female)"]
  + = female pin header, 1 pin [form="♀ (female)"]
  ground = female pin header, 1 pin [form="♀ (female)"]

nets:
  N1: R1.Pin_0, J2.pin4
  N2: R1.Pin_1, Q1.B
  N3: R2.Pin_0, LED1.anode
  N4: R2.Pin_1, J1.pin8, +.pin1
  N5: LED1.cathode, Q1.C
  GND: Q1.E, J2.pin8, ground.pin1
